// Logisim project a1-template.circ as structural Verilog: 5 circuits, main circuit main
// L1
module main (
  input  M0,
  input  E0,
  input  E1,
  input  M1
);

  wire [1:0] L0_l1, r0_1_out_5;
  wire [4:0] rom_2_data, rom_2_data_2;
  wire [14:0] rom_1_data;
  wire [14:10] rom_2_data_3;

  L0 L0 (.in_1(M0), .in_2(M1), .in_3(E0), .in_4(E1), .L1(L0_l1[0]));
  L1 l1_1 (.Mo(M0), .M1(M1), .E0(E0), .E1(E1), .out_5(L0_l1[1]));
  R0 r0_1 (.M0(M0), .M1(M1), .E0(E0), .E1(E1), .out_5(r0_1_out_5[0]));
  R1 r1_1 (.M0(M0), .M1(M1), .E0(E0), .E1(E1), .out_5(r0_1_out_5[1]));
  DotMatrix #(.matrixcols(3), .matrixrows(5)) dotmatrix_1 (
    .col0(rom_1_data[14:10]), .col1(rom_1_data[9:5]), .col2(rom_1_data[4:0]));
  ROM #(.addrWidth(2), .dataWidth(15)) rom_1 (.addr(L0_l1), .data(rom_1_data));  // open: sel
  ROM #(.addrWidth(2), .dataWidth(15)) rom_2 (
    .addr(r0_1_out_5), .data({rom_2_data_3, rom_2_data_2, rom_2_data}));  // open: sel
  DotMatrix #(.matrixcols(3), .matrixrows(5)) dotmatrix_2 (.col0(rom_2_data_3), .col1(rom_2_data_2), .col2(rom_2_data));

  // Notes on the sheet:
  //   Sensors
  //   L1
  //     R0
  //   R1
  //   L1
  //   L0
  //   R1
  //   R0
  //   Motor Controller
  //   left
  //   contents of rom_1 (hex, n*v repeats v):
  //   1084 2308 862 288a
  //   contents of rom_2 (hex, n*v repeats v):
  //   1084 2308 862 288a
  //   right
  //   forward
  //   stopped
  //   reverse
endmodule

module L0 (
  input  in_1,
  input  in_2,
  input  in_3,
  input  in_4,
  output L1
);

  wire and_1_out, and_2_out, and_3_out, not_1_out, not_2_out;

  not not_1 (not_1_out, in_1);
  not not_2 (not_2_out, in_3);
  and and_1 (and_1_out, in_1, in_2);
  and and_2 (and_2_out, not_1_out, not_2_out);
  and and_3 (and_3_out, not_1_out, in_4);
  or or_1 (L1, and_1_out, and_2_out, and_3_out);

  // Notes on the sheet:
  //   M0
  //   M1
  //   E0
  //   E1
endmodule

module L1 (
  input  Mo,
  input  M1,
  input  E0,
  input  E1,
  output out_5
);

  wire and_1_out, and_2_out, not_1_out, not_2_out;

  not not_1 (not_1_out, M1);
  not not_2 (not_2_out, E0);
  and and_1 (and_1_out, Mo, not_1_out, not_2_out);
  and and_2 (and_2_out, Mo, not_1_out, E1);
  or or_1 (out_5, and_1_out, and_2_out);
endmodule

module R0 (
  input  M0,
  input  M1,
  input  E0,
  input  E1,
  output out_5
);

  wire and_1_out, and_2_out, not_1_out, not_2_out;

  not not_1 (not_1_out, M0);
  not not_2 (not_2_out, E1);
  and and_1 (and_1_out, not_1_out, not_2_out);
  and and_2 (and_2_out, not_1_out, E0);
  or or_1 (out_5, and_2_out, and_1_out);
endmodule

module R1 (
  input  M0,
  input  M1,
  input  E0,
  input  E1,
  output out_5
);

  wire and_1_out, and_2_out, and_3_out, not_1_out, not_2_out;

  not not_1 (not_1_out, E0);
  not not_2 (not_2_out, E1);
  and and_1 (and_1_out, M0, E0);
  and and_2 (and_2_out, M0, not_2_out);
  and and_3 (and_3_out, M0, M1, not_1_out);
  or or_1 (out_5, and_1_out, and_2_out, and_3_out);
endmodule
