// Logisim project a2-template.circ as structural Verilog: 1 circuit, main circuit main
module main (
  input  Start
);

  wire Master_clock_out;
  wire [3:0] comparator_1_lt;
  wire [6:0] rom_1_data;
  wire [31:0] adder_1_out, multiplexer_1_out, multiplexer_2_out, register_1_q, register_2_q, register_3_q,
       subtractor_1_out;

  Subtractor #(.width(32)) subtractor_1 (
    .a(register_1_q), .b(register_2_q), .out(subtractor_1_out));  // open: bin, bout
  Button u_Start (.out(comparator_1_lt[1]));
  Multiplexer #(.width(32)) multiplexer_1 (
    .in0(32'he1), .in1(subtractor_1_out), .out(multiplexer_1_out), .sel(rom_1_data[4]));  // open: en
  Register #(.width(32)) register_1 (.D(multiplexer_1_out), .Q(register_1_q), .clk(rom_1_data[2]));  // open: en, clr
  Comparator #(.width(32)) comparator_1 (.a(register_1_q), .b(register_2_q), .lt(comparator_1_lt[0]));  // open: gt, eq
  Clock Master_clock (.out(Master_clock_out));
  Register #(.width(32)) register_2 (.D(32'ha), .Q(register_2_q), .clk(rom_1_data[1]));  // open: en, clr
  ROM #(.addrWidth(4), .dataWidth(7)) rom_1 (.addr(comparator_1_lt), .data(rom_1_data));  // open: sel
  Button Reset ();  // open: out
  Button Single_step ();  // open: out
  T_Flip_Flop t_ff_1 (
    .clk(Master_clock_out), .T(rom_1_data[6]), .Q(comparator_1_lt[3]));  // open: Qn, preset, reset, en
  T_Flip_Flop t_ff_2 (
    .clk(Master_clock_out), .T(rom_1_data[5]), .Q(comparator_1_lt[2]));  // open: Qn, preset, reset, en
  Adder #(.width(32)) adder_1 (.a(register_3_q), .b(32'h1), .out(adder_1_out));  // open: cin, cout
  Multiplexer #(.width(32)) multiplexer_2 (
    .in0({32{1'b0}}), .in1(adder_1_out), .out(multiplexer_2_out), .sel(rom_1_data[3]));  // open: en
  Register #(.width(32)) register_3 (.D(multiplexer_2_out), .Q(register_3_q), .clk(rom_1_data[0]));  // open: en, clr

  // Notes on the sheet:
  //   a
  //   a<b
  //   b
  //   contents of rom_1 (hex, n*v repeats v):
  //   0 0 27 27 7d 40 7d 40 78 20 78 20
  //   x
endmodule
