// Logisim project a22-template.circ as structural Verilog: 1 circuit, main circuit main
module main (
  input  in_1,
  input  Start,
  output [31:0] out_3,
  output [31:0] out_4,
  output out_5,
  output out_6,
  output out_7,
  output out_8,
  output out_9,
  output out_10,
  output out_11
);

  wire Master_clock_out;
  wire [3:0] Start_out;
  wire [3:3] rom_1_data;
  wire [31:0] adder_1_out, multiplexer_1_out, multiplexer_2_out, register_1_q, subtractor_1_out;

  Subtractor #(.width(32)) subtractor_1 (.a(register_1_q), .b(out_3), .out(subtractor_1_out));  // open: bin, bout
  Button u_Start (.out(Start_out[0]));
  Multiplexer #(.width(32)) multiplexer_1 (
    .in0(32'he1), .in1(subtractor_1_out), .out(multiplexer_1_out), .sel(out_6));  // open: en
  Register #(.width(32)) register_1 (.D(multiplexer_1_out), .Q(register_1_q), .clk(out_5));  // open: en, clr
  Comparator #(.width(32)) comparator_1 (.a(register_1_q), .b(out_3), .lt(Start_out[1]));  // open: gt, eq
  ROM #(.addrWidth(4)) rom_1 (
    .addr(Start_out), .data({out_11, out_10, out_9, out_8, rom_1_data[3], out_7, out_6, out_5}));  // open: sel
  Clock Master_clock (.out(Master_clock_out));
  Register #(.width(32)) register_2 (.D(32'ha), .Q(out_3), .clk(out_5));  // open: en, clr
  D_Flip_Flop d_ff_1 (.clk(Master_clock_out), .D(out_8), .Q(Start_out[2]));  // open: Qn, preset, en, reset
  D_Flip_Flop d_ff_2 (.clk(Master_clock_out), .D(out_9), .Q(Start_out[3]));  // open: Qn, preset, en, reset
  Button Reset ();  // open: out
  Button Single_step ();  // open: out
  Adder #(.width(32)) adder_1 (.a(out_4), .b(32'h1), .out(adder_1_out));  // open: cin, cout
  Multiplexer #(.width(32)) multiplexer_2 (
    .in0({32{1'b0}}), .in1(adder_1_out), .out(multiplexer_2_out), .sel(out_6));  // open: en
  Register #(.width(32)) register_3 (.D(multiplexer_2_out), .Q(out_4), .clk(out_5));  // open: en, clr

  // Notes on the sheet:
  //   a
  //   0 = X0 start 
  //   1 = X1 a<b
  //   2 = Y0 state
  //   3 = Y1 state
  //   a<b
  //   contents of rom_1 (hex, n*v repeats v):
  //   0 13 0 0 22 10 30 10 11 20 30 20
  //   b
  //   0 = Z0 a b x register enabled
  //   1 = Z1 multipler a x enbled
  //   5 = Y1 next state
  //   x
  //   4 = Y0 next state
endmodule
