// Logisim project Enable latch.circ as structural Verilog: 1 circuit, main circuit main
module main (
  input  s,
  input  eN,
  input  R,
  output out_4,
  output out_5
);

  wire nand_1_out, nand_2_out;

  nand nand_1 (nand_1_out, s, eN);
  nand nand_2 (nand_2_out, eN, R);
  nand nand_3 (out_4, nand_1_out, out_5);
  nand nand_4 (out_5, out_4, nand_2_out);
endmodule
