// Logisim project Basic Gates - Exercise 1.2.circ as structural Verilog: 1 circuit, main circuit main
module main (
  input  A,
  input  B,
  input  C,
  output D
);

  wire and_1_out, not_1_out, not_2_out, not_3_out, or_1_out;

  not not_1 (not_1_out, B);
  not not_2 (not_2_out, A);
  not not_3 (not_3_out, and_1_out);
  and and_1 (and_1_out, A, not_1_out);
  or or_1 (or_1_out, B, not_2_out, C);
  and and_2 (D, not_3_out, or_1_out);
endmodule
