// Logisim project Basic Gates - Exercise 2 - optimized.circ as structural Verilog: 1 circuit, main circuit main
module main (
  input  A,
  input  B,
  input  C,
  output D
);

  wire nor_1_out, nor_2_out, nor_3_out, nor_4_out;

  nor nor_1 (nor_1_out, A, A);
  nor nor_2 (nor_2_out, B, B);
  nor nor_3 (nor_3_out, nor_2_out, C);
  nor nor_4 (nor_4_out, nor_1_out, B);
  nor nor_5 (D, nor_4_out, nor_3_out);
endmodule
