// Logisim project Latches and FlipFlops - Exercise 1.circ as structural Verilog: 3 circuits, main circuit main
module main (
  input  Select_0,
  input  Select_1,
  input  Data,
  output Q0,
  output Q1,
  output Q2,
  output Q3
);

  wire Decoder_select_0, Decoder_select_1, Decoder_select_2, Decoder_select_3;

  _2bit_Decoder Decoder (
    .In_0(Select_0), .In_1(Select_1), .Select_0(Decoder_select_0), .Select_1(Decoder_select_1),
    .Select_2(Decoder_select_2), .Select_3(Decoder_select_3));
  D_Latch Latch_0 (.D(Data), .E(Decoder_select_0), .Q(Q0));  // open: minus_Q
  D_Latch Latch_1 (.D(Data), .E(Decoder_select_1), .Q(Q1));  // open: minus_Q
  D_Latch Latch_2 (.D(Data), .E(Decoder_select_2), .Q(Q2));  // open: minus_Q
  D_Latch Latch_3 (.D(Data), .E(Decoder_select_3), .Q(Q3));  // open: minus_Q
endmodule

module D_Latch (
  input  D,
  input  E,
  output minus_Q,
  output Q
);

  wire and_1_out, and_2_out, not_1_out;

  not not_1 (not_1_out, D);
  and and_1 (and_1_out, D, E);
  and and_2 (and_2_out, E, not_1_out);
  nor nor_1 (minus_Q, and_1_out, Q);
  nor nor_2 (Q, minus_Q, and_2_out);

  // Notes on the sheet:
  //   E: pull=down
  //   D: pull=down
  //   Q: pull=down
  //   minus_Q: pull=down
endmodule

module _2bit_Decoder (
  input  In_0,
  input  In_1,
  output Select_0,
  output Select_1,
  output Select_2,
  output Select_3
);

  wire not_1_out, not_2_out;

  not not_1 (not_1_out, In_0);
  not not_2 (not_2_out, In_1);
  and and_1 (Select_0, not_1_out, not_2_out);
  and and_2 (Select_1, In_0, not_2_out);
  and and_3 (Select_2, In_1, not_1_out);
  and and_4 (Select_3, In_0, In_1);

  // Notes on the sheet:
  //   In_0: pull=down
  //   In_1: pull=down
endmodule
