// Logisim project DL1.circ as structural Verilog: 4 circuits, main circuit xor
module \xor  (
  input  X,
  input  Y
);

  wire and_1_out, and_2_out, not_1_out, not_2_out, or_1_out;

  not not_1 (not_1_out, Y);
  not not_2 (not_2_out, X);
  and and_1 (and_1_out, X, not_1_out);
  and and_2 (and_2_out, not_2_out, Y);
  or or_1 (or_1_out, and_1_out, and_2_out);
  LED led_1 (.in(or_1_out));
endmodule

module xor1 (
  input  X,
  input  Y
);

  wire and_1_out, and_2_out, not_1_out, or_1_out;

  or or_1 (or_1_out, X, Y);
  and and_1 (and_1_out, X, Y);
  not not_1 (not_1_out, and_1_out);
  and and_2 (and_2_out, or_1_out, not_1_out);
  LED led_1 (.in(and_2_out));
endmodule

module Example1_Function (
  input  x,
  input  y,
  input  z
);

  wire and_1_out, not_1_out, not_2_out, not_3_out, or_1_out;

  not not_1 (not_1_out, x);
  not not_2 (not_2_out, y);
  not not_3 (not_3_out, z);
  and and_1 (and_1_out, not_1_out, not_2_out);
  or or_1 (or_1_out, and_1_out, not_3_out);
  LED led_1 (.in(or_1_out));
endmodule

module Example2_Function (
  input  in_1,
  input  in_2,
  input  in_3,
  input  in_4
);

  wire and_1_out, not_1_out, not_2_out, or_1_out, xor_1_out, xor_2_out;

  xor xor_1 (xor_1_out, in_1, in_2);
  not not_1 (not_1_out, in_3);
  not not_2 (not_2_out, in_4);
  and and_1 (and_1_out, xor_1_out, not_1_out);
  or or_1 (or_1_out, not_1_out, in_4);
  ExactlyOne xor_2 (.out(xor_2_out), .in0(and_1_out), .in1(not_2_out), .in2(or_1_out));
  LED led_1 (.in(xor_2_out));
endmodule
