// Logisim project DL2.circ as structural Verilog
module HA (
  input  x,
  input  y,
  output Sum,
  output Carry
);

  xor xor_1 (Sum, x, y);
  and and_1 (Carry, x, y);
endmodule

module FA (
  input  x,
  input  y,
  input  z,
  output Sum,
  output Carry_Out
);

  wire and_1_out, and_2_out, xor_1_out;

  xor xor_1 (xor_1_out, y, z);
  and and_1 (and_1_out, y, z);
  xor xor_2 (Sum, x, xor_1_out);
  and and_2 (and_2_out, x, xor_1_out);
  or or_1 (Carry_Out, and_2_out, and_1_out);
endmodule

module _2_4_Decoder (
  input  I0,
  input  I1,
  output F0,
  output F1,
  output F2,
  output F3
);

  wire not_1_out, not_2_out;

  not not_1 (not_1_out, I0);
  not not_2 (not_2_out, I1);
  and and_1 (F0, not_1_out, not_1_out, not_2_out);
  and and_2 (F1, not_1_out, I1);
  and and_3 (F2, I0, not_2_out);
  and and_4 (F3, I0, I1);
endmodule

module Logic_Unit (
  input  x,
  input  y,
  output xy,
  output x_y,
  output y_prime
);

  and and_1 (xy, x, y);
  or or_1 (x_y, x, y);
  not not_1 (y_prime, y);
endmodule

module Bit_Slice (
  input  x,
  input  y,
  input  ci,
  input  f0,
  input  f1,
  output Output,
  output Carry_out
);

  wire and_1_out, and_2_out, and_3_out, and_4_out, Decoder_f0, Decoder_f1, Decoder_f2, Decoder_f3,
       Full_Adder_carry_out, Full_Adder_sum, Logic_Unit_x_y, Logic_Unit_xy, Logic_Unit_y_prime;

  Logic_Unit Logic_Unit (.x(x), .y(y), .xy(Logic_Unit_xy), .x_y(Logic_Unit_x_y), .y_prime(Logic_Unit_y_prime));
  FA Full_Adder (.y(y), .z(ci), .x(x), .Sum(Full_Adder_sum), .Carry_Out(Full_Adder_carry_out));
  _2_4_Decoder Decoder (.I0(f0), .I1(f1), .F0(Decoder_f0), .F1(Decoder_f1), .F2(Decoder_f2), .F3(Decoder_f3));
  and and_1 (and_1_out, Logic_Unit_xy, Decoder_f0);
  and and_2 (and_2_out, Logic_Unit_x_y, Decoder_f1);
  and and_3 (and_3_out, Logic_Unit_y_prime, Decoder_f2);
  and and_4 (and_4_out, Full_Adder_sum, Decoder_f3);
  and and_5 (Carry_out, Full_Adder_carry_out, Decoder_f3);
  or or_1 (Output, and_1_out, and_2_out, and_3_out, and_4_out);
endmodule

module _4_bit_ALU (
  input  x,
  input  in_2,
  input  y,
  input  in_4,
  input  in_5,
  input  in_6,
  input  in_7,
  input  in_8,
  input  Carry_in,
  input  Function,
  input  in_11,
  output out_12,
  output Output,
  output out_14,
  output out_15,
  output Carry_out
);

  wire Bit_Slice_2_carry_out, Bit_Slice_3_carry_out, Bit_Slice_carry_out;

  Bit_Slice Bit_Slice (
    .x(in_4), .y(in_8), .ci(Carry_in), .f0(Function), .f1(in_11), .Output(out_15),
    .Carry_out(Bit_Slice_carry_out));
  Bit_Slice Bit_Slice_2 (
    .x(y), .y(in_7), .ci(Bit_Slice_carry_out), .f0(Function), .f1(in_11), .Output(out_14),
    .Carry_out(Bit_Slice_2_carry_out));
  Bit_Slice Bit_Slice_3 (
    .x(in_2), .y(in_6), .ci(Bit_Slice_2_carry_out), .f0(Function), .f1(in_11), .Output(Output),
    .Carry_out(Bit_Slice_3_carry_out));
  Bit_Slice Bit_Slice_4 (
    .x(x), .y(in_5), .ci(Bit_Slice_3_carry_out), .f0(Function), .f1(in_11), .Output(out_12),
    .Carry_out(Carry_out));
endmodule

module _4_input_Multiplexer (
  input  in_1,
  input  in_2,
  input  in_3,
  input  in_4,
  input  in_5,
  input  in_6
);

  wire and_1_out, and_2_out, and_3_out, and_4_out, not_1_out, not_2_out, or_1_out;

  not not_1 (not_1_out, in_1);
  not not_2 (not_2_out, in_2);
  and and_1 (and_1_out, in_3, not_1_out, not_2_out);
  and and_2 (and_2_out, in_4, not_1_out, in_2);
  and and_3 (and_3_out, in_5, not_2_out, in_1);
  and and_4 (and_4_out, in_6, in_1, in_2);
  or or_1 (or_1_out, and_1_out, and_2_out, and_3_out, and_4_out);
  LED led_1 (.in(or_1_out));
endmodule

module _4_bit_Comparator (
  input  x,
  input  in_2,
  input  y,
  input  in_4,
  input  in_5,
  input  in_6,
  input  in_7,
  input  in_8,
  output out_9
);

  wire xor_1_out, xor_2_out, xor_3_out, xor_4_out;

  xor xor_1 (xor_1_out, in_8, in_4);
  xor xor_2 (xor_2_out, in_7, y);
  xor xor_3 (xor_3_out, in_6, in_2);
  xor xor_4 (xor_4_out, in_5, x);
  nor nor_1 (out_9, xor_1_out, xor_2_out, xor_3_out, xor_4_out);
endmodule

module _4_bit_Adder (
  input  x,
  input  in_2,
  input  in_3,
  input  in_4,
  input  y,
  input  in_6,
  input  in_7,
  input  in_8,
  output out_9,
  output out_10,
  output out_11,
  output out_12,
  output out_13
);

  wire fa_1_p5, fa_2_p5, ha_1_carry;

  HA ha_1 (.x(in_4), .y(in_8), .Sum(out_13), .Carry(ha_1_carry));
  // FA fa_1: pin names not known; wires that end beside it: in_3, in_7, ha_1_carry, out_12, fa_1_p5
  // FA fa_2: pin names not known; wires that end beside it: in_2, in_6, fa_1_p5, out_11, fa_2_p5
  // FA fa_3: pin names not known; wires that end beside it: x, y, fa_2_p5, out_10, out_9
endmodule
