// Logisim project DL3.circ as structural Verilog: 10 circuits, main circuit Clocked - SR
module Clocked___SR (
  input  S,
  input  R,
  output Q_prime,
  output Q
);

  wire and_1_out, and_2_out, clock_1_out;

  Clock clock_1 (.out(clock_1_out));
  and and_1 (and_1_out, S, clock_1_out);
  and and_2 (and_2_out, clock_1_out, R);
  nor nor_1 (Q_prime, and_1_out, Q);
  nor nor_2 (Q, Q_prime, and_2_out);
endmodule

module D_Latch (
  input  in_1,
  output Q,
  output Q_prime
);

  wire and_1_out, and_2_out, clock_1_out, not_1_out;

  Clock clock_1 (.out(clock_1_out));
  not not_1 (not_1_out, in_1);
  and and_1 (and_1_out, not_1_out, clock_1_out);
  and and_2 (and_2_out, clock_1_out, in_1);
  nor nor_1 (Q, and_1_out, Q_prime);
  nor nor_2 (Q_prime, Q, and_2_out);
endmodule

module NAND_SR_latch (
);

  wire nand_1_out, nand_2_out, R_out, S_out;

  Button S (.out(S_out));
  Button R (.out(R_out));
  nand nand_1 (nand_1_out, S_out, nand_2_out);
  nand nand_2 (nand_2_out, nand_1_out, R_out);
  LED Q_prime (.in(nand_1_out));
  LED Q (.in(nand_2_out));
endmodule

module D_Flip_Flop (
  input  in_1,
  output out_2
);

  wire clock_1_out, d_latch_2_1_q, not_1_out;

  Clock clock_1 (.out(clock_1_out));
  D_Latch_2 d_latch_2_1 (.Clock(in_1), .in_2(clock_1_out), .Q(d_latch_2_1_q));  // open: Q_prime
  not not_1 (not_1_out, clock_1_out);
  D_Latch_2 d_latch_2_2 (.Clock(d_latch_2_1_q), .in_2(not_1_out), .Q(out_2));  // open: Q_prime
endmodule

module D_Latch_2 (
  input  Clock,
  input  in_2,
  output Q,
  output Q_prime
);

  wire and_1_out, and_2_out, not_1_out;

  not not_1 (not_1_out, in_2);
  and and_1 (and_1_out, not_1_out, Clock);
  and and_2 (and_2_out, Clock, in_2);
  nor nor_1 (Q, and_1_out, Q_prime);
  nor nor_2 (Q_prime, Q, and_2_out);
endmodule

module AC_Combinational (
  input  P,
  input  S,
  input  A,
  input  B,
  output X,
  output Y
);

  wire and_1_out, and_2_out, and_3_out, and_4_out, not_1_out, not_2_out, not_3_out, not_4_out, or_1_out,
       xor_1_out;

  not not_1 (not_1_out, P);
  not not_2 (not_2_out, S);
  not not_3 (not_3_out, A);
  not not_4 (not_4_out, B);
  xor xor_1 (xor_1_out, P, B);
  and and_1 (and_1_out, xor_1_out, not_2_out, not_3_out);
  and and_2 (and_2_out, not_1_out, S, A, not_4_out);
  and and_3 (and_3_out, S, not_3_out, B);
  and and_4 (and_4_out, not_2_out, A, not_4_out);
  or or_1 (or_1_out, and_3_out, and_4_out);
  or or_2 (Y, and_1_out, and_2_out);
  and and_5 (X, not_1_out, or_1_out);
endmodule

module AC_Sequential (
  input  P,
  input  S,
  output X,
  output Y
);

  wire d_ff_1_q, d_ff_2_q, nor_1_out;

  AC_Combinational ac_combinational_1 (.P(P), .S(S), .A(d_ff_1_q), .B(d_ff_2_q), .Y(Y), .X(X));
  nor nor_1 (nor_1_out, P, S);
  D_Flip_Flop_part d_ff_1 (.clk(nor_1_out), .D(X), .Q(d_ff_1_q));  // open: Qn, preset, en, reset
  D_Flip_Flop_part d_ff_2 (.clk(nor_1_out), .D(Y), .Q(d_ff_2_q));  // open: Qn, preset, en, reset
endmodule

module AC_System_2 (
  input  Power,
  input  Speed,
  output out_3,
  output out_4,
  output out_5,
  output out_6
);

  wire AC_x, AC_y, not_1_out;

  AC_Sequential AC (.X(AC_x), .Y(AC_y), .P(Power), .S(Speed));
  xor xor_1 (out_3, AC_x, AC_y);
  not not_1 (not_1_out, AC_y);
  and and_1 (out_5, not_1_out, AC_x);

  assign out_4 = out_3;
  assign out_6 = out_5;
endmodule

module AC_System (
  output out_1,
  output out_2,
  output out_3,
  output out_4
);

  wire ac_sequential_1_x, ac_sequential_1_y, not_1_out, Power_out, Speed_out;

  Button Power (.out(Power_out));
  Button Speed (.out(Speed_out));
  AC_Sequential ac_sequential_1 (.X(ac_sequential_1_x), .Y(ac_sequential_1_y), .P(Power_out), .S(Speed_out));
  xor xor_1 (out_1, ac_sequential_1_x, ac_sequential_1_y);
  not not_1 (not_1_out, ac_sequential_1_y);
  and and_1 (out_3, not_1_out, ac_sequential_1_x);

  assign out_2 = out_1;
  assign out_4 = out_3;
endmodule

module Timer (
  output A,
  output B
);

  wire and_1_out, and_2_out, clock_1_out, d_ff_1_q, d_ff_2_q, not_1_out, not_2_out, not_3_out, not_4_out,
       not_5_out, xor_1_out;

  Clock clock_1 (.out(clock_1_out));
  not not_1 (not_1_out, d_ff_1_q);
  not not_2 (not_2_out, d_ff_2_q);
  not not_3 (not_3_out, clock_1_out);
  not not_4 (not_4_out, clock_1_out);
  not not_5 (not_5_out, clock_1_out);
  and and_1 (and_1_out, d_ff_2_q, not_1_out, clock_1_out);
  and and_2 (and_2_out, not_2_out, not_3_out, d_ff_1_q);
  xor xor_1 (xor_1_out, d_ff_2_q, clock_1_out);
  D_Flip_Flop_part d_ff_1 (.clk(not_4_out), .D(A), .Q(d_ff_1_q));  // open: Qn, preset, en, reset
  D_Flip_Flop_part d_ff_2 (.clk(not_5_out), .D(B), .Q(d_ff_2_q));  // open: Qn, preset, en, reset
  or or_1 (A, and_1_out, and_2_out);
  and and_3 (B, not_1_out, xor_1_out);

  // Notes on the sheet:
  //   A
  //   B
endmodule
